# Fritzing sketch pi-hydro1 (saved by Fritzing 0.9.3b)

parts:
  J13 = female pin header, 6 pins [form="♀ (female)"]
  J14 = female pin header, 6 pins [form="♀ (female)"]  # not connected
  J18 = female pin header, 5 pins [form="♀ (female)"]
  Raspberry_Pi_1 = Raspberry Pi 3 [part_number=RPI-3-V1.2]  # not connected
  J19 = female pin header, 5 pins [form="♀ (female)"]
  J20 = female pin header, 5 pins [form="♀ (female)"]  # not connected
  J21 = female pin header, 5 pins [form="♀ (female)"]  # not connected
  J22 = female pin header, 3 pins [form="♀ (female)"]
  J23 = female pin header, 3 pins [form="♀ (female)"]
  J24 = female pin header, 3 pins [form="♀ (female)"]
  J25 = female pin header, 3 pins [form="♀ (female)"]
  J26 = female pin header, 3 pins [form="♀ (female)"]
  J27 = female pin header, 5 pins [form="♀ (female)"]
  J28 = female pin header, 3 pins [form="♀ (female)"]
  J29 = female pin header, 3 pins [form="♀ (female)"]
  J30 = female pin header, 3 pins [form="♀ (female)"]
  J31 = female pin header, 3 pins [form="♀ (female)"]
  J32 = female pin header, 5 pins [form="♀ (female)"]
  J33 = female pin header, 2 pins [form="♀ (female)"]
  J34 = female pin header, 3 pins [form="♀ (female)"]
  J35 = female pin header, 5 pins [form="♀ (female)"]
  J36 = female pin header, 2 pins [form="♀ (female)"]
  J37 = female pin header, 2 pins [form="♀ (female)"]
  J38 = female pin header, 2 pins [form="♀ (female)"]
  J39 = female pin header, 2 pins [form="♀ (female)"]
  J40 = female pin header, 5 pins [form="♀ (female)"]
  J41 = female pin header, 3 pins [form="♀ (female)"]
  J42 = female pin header, 3 pins [form="♀ (female)"]
  J43 = female pin header, 3 pins [form="♀ (female)"]

nets:
  N1: J13.pin3, J18.pin5
  N2: J13.pin4, J18.pin3
  N3: J13.pin5, J18.pin2
  N4: J13.pin6, J18.pin1
  N5: J19.pin1, J28.pin1, J28.pin2
  N6: J19.pin2, J31.pin1, J31.pin2
  N7: J19.pin3, J30.pin2
  N8: J19.pin4, J29.pin2
  N9: J19.pin5, J22.pin3
  N10: J22.pin1, J32.pin5
  N11: J22.pin2, J27.pin5
  N12: J23.pin1, J32.pin4
  N13: J23.pin2, J27.pin4
  N14: J23.pin3, J29.pin3
  N15: J24.pin1, J32.pin3
  N16: J24.pin2, J27.pin3
  N17: J24.pin3, J30.pin3
  N18: J25.pin1, J32.pin2
  N19: J25.pin2, J27.pin2
  N20: J25.pin3, J31.pin3
  N21: J26.pin1, J32.pin1
  N22: J26.pin2, J27.pin1
  N23: J26.pin3, J28.pin3
  N24: J33.pin1, J35.pin5
  N25: J33.pin2, J40.pin5
  N26: J34.pin2, J40.pin4
  N27: J34.pin3, J36.pin2
  N28: J35.pin1, J39.pin1
  N29: J35.pin2, J38.pin1
  N30: J35.pin3, J37.pin1
  N31: J35.pin4, J36.pin1
  N32: J37.pin2, J41.pin3
  N33: J38.pin2, J42.pin3
  N34: J39.pin2, J43.pin3
  N35: J40.pin1, J43.pin2
  N36: J40.pin2, J42.pin2
  N37: J40.pin3, J41.pin2

notes:
  EZO PH
  EZO EC
  EZO RTD
  EZO DO
  Tentacle T3
  Isolated Carrier
  Whitebox Tentacle T3
  Atlas Scientific Electrically Isolated EZO Carrier Board
  EZO RTD I2C 0x66
  EZO PH I2C 0x63
  EZO EC I2C 0x64
  EZO DO I2C 0x61
  Channel 5 is a spare. The I2C hub is used to connect to other modules.
  Sequent Microsystems
  8 Relay HAT I2C 0x27
  24V DC
  120 VAC
