# Fritzing sketch pi-hydro2 (saved by Fritzing 0.9.10b)

parts:
  J13 = female pin header, 6 pins [form="♀ (female)"]
  J14 = female pin header, 6 pins [form="♀ (female)"]
  J18 = female pin header, 5 pins [form="♀ (female)"]
  J19 = female pin header, 5 pins [form="♀ (female)"]
  J20 = female pin header, 5 pins [form="♀ (female)"]  # not connected
  J21 = female pin header, 5 pins [form="♀ (female)"]  # not connected
  J22 = female pin header, 3 pins [form="♀ (female)"]
  J23 = female pin header, 3 pins [form="♀ (female)"]
  J24 = female pin header, 3 pins [form="♀ (female)"]
  J25 = female pin header, 3 pins [form="♀ (female)"]
  J26 = female pin header, 3 pins [form="♀ (female)"]
  J27 = female pin header, 5 pins [form="♀ (female)"]
  J28 = female pin header, 3 pins [form="♀ (female)"]
  J29 = female pin header, 3 pins [form="♀ (female)"]
  J30 = female pin header, 3 pins [form="♀ (female)"]
  J31 = female pin header, 3 pins [form="♀ (female)"]
  J32 = female pin header, 5 pins [form="♀ (female)"]
  J33 = female pin header, 2 pins [form="♀ (female)"]
  J34 = female pin header, 3 pins [form="♀ (female)"]
  J35 = female pin header, 5 pins [form="♀ (female)"]
  J36 = female pin header, 2 pins [form="♀ (female)"]
  J37 = female pin header, 2 pins [form="♀ (female)"]
  J38 = female pin header, 2 pins [form="♀ (female)"]
  J39 = female pin header, 2 pins [form="♀ (female)"]
  J40 = female pin header, 5 pins [form="♀ (female)"]
  J41 = female pin header, 3 pins [form="♀ (female)"]
  J42 = female pin header, 3 pins [form="♀ (female)"]
  J43 = female pin header, 3 pins [form="♀ (female)"]
  Mod1 = Raspberry Pi 4B  # not connected
  Part1 = Adafruit SCD4x [part_number="Adafruit #5187"]

nets:
  N1: J13.pin3, J18.pin5
  N2: J13.pin4, J18.pin3
  N3: J13.pin5, J18.pin2
  N4: J13.pin6, J18.pin1
  N5: J14.pin3, Part1.VCC
  N6: J14.pin4, Part1.GND
  N7: J14.pin5, Part1.SDA
  N8: J14.pin6, Part1.SCL
  N9: J19.pin1, J28.pin1, J28.pin2
  N10: J19.pin2, J31.pin1, J31.pin2
  N11: J19.pin3, J30.pin2
  N12: J19.pin4, J29.pin2
  N13: J19.pin5, J22.pin3
  N14: J22.pin1, J32.pin5
  N15: J22.pin2, J27.pin5
  N16: J23.pin1, J32.pin4
  N17: J23.pin2, J27.pin4
  N18: J23.pin3, J29.pin3
  N19: J24.pin1, J32.pin3
  N20: J24.pin2, J27.pin3
  N21: J24.pin3, J30.pin3
  N22: J25.pin1, J32.pin2
  N23: J25.pin2, J27.pin2
  N24: J25.pin3, J31.pin3
  N25: J26.pin1, J32.pin1
  N26: J26.pin2, J27.pin1
  N27: J26.pin3, J28.pin3
  N28: J33.pin1, J35.pin5
  N29: J33.pin2, J40.pin5
  N30: J34.pin2, J40.pin4
  N31: J34.pin3, J36.pin2
  N32: J35.pin1, J39.pin1
  N33: J35.pin2, J38.pin1
  N34: J35.pin3, J37.pin1
  N35: J35.pin4, J36.pin1
  N36: J37.pin2, J41.pin3
  N37: J38.pin2, J42.pin3
  N38: J39.pin2, J43.pin3
  N39: J40.pin1, J43.pin2
  N40: J40.pin2, J42.pin2
  N41: J40.pin3, J41.pin2

notes:
  EZO PH
  EZO EC
  EZO RTD
  EZO DO
  Tentacle T3
  Isolated Carrier
  Whitebox Tentacle T3
  Atlas Scientific Electrically Isolated EZO Carrier Board
  EZO RTD I2C 0x66
  EZO PH I2C 0x63
  EZO EC I2C 0x64
  EZO DO I2C 0x61
  Sequent Microsystems
  8 Relay HAT I2C 0x27
  SCD41 I2C 0x62
  24V DC
  120 VAC
  24V DC or 120 VAC

custom parts:
  Adafruit SCD4x: Take a deep breath in...now slowly breathe out. Mmm isn't it wonderful? All that air around us, which we bring into our lungs, extracts oxygen from and then breathes out carbon dioxide. CO2 is essential for life on this planet we call Earth - we and plants take turns using and emitting CO2 in an elegant symbiosis. But it's important to keep that CO2 balanced - you don't want too much around,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
